# Fritzing sketch LPC1114 (saved by Fritzing 0.9.3b)
breadboards: 1

parts:
  IC1 = LPC1114 [package=DIL]
  R1 = Resistor [tolerance=±5% resistance=1k package=THT]
  LED1 = LED - 5mm [color="Red (633nm)" package="5 mm [THT]"]
  パーツ1 = FTDI Basic Programmer
  S1 = Pushbutton [package="[THT]"]
  S2 = Pushbutton [package="[THT]"]
  R2 = Resistor [tolerance=±5% resistance=330 package=THT]
  R3 = Resistor [tolerance=±5% resistance=10k package=THT]

nets:
  N1: IC1.D1_5, R1.Pin_0
  N2: IC1.D1_6/RXD, パーツ1.TXO
  N3: IC1.D1_7/TXD, パーツ1.RXI
  N4: IC1.VCC, パーツ1.POWER, R3.Pin_1
  GND: IC1.GND, LED1.cathode, パーツ1.GND, S1.Pin_3, S1.Pin_4, R2.Pin_1
  N5: IC1.D0_0/RESET, S1.Pin_1, S1.Pin_2, R3.Pin_0
  N6: IC1.D0_1, S2.Pin_1, S2.Pin_2
  N7: R1.Pin_1, LED1.anode
  N8: S2.Pin_3, S2.Pin_4, R2.Pin_0

notes:
  #RESET(dp23) - DTR
  PIO0_1(dp24) - RTS
