# Fritzing sketch RPi_LPC1114 (saved by Fritzing 0.9.3b)
breadboards: 1

parts:
  Raspberry_Pi1 = Raspberry Pi B+
  IC1 = LPC1114 [package=DIL]
  R1 = Resistor [tolerance=±5% resistance=10k package=THT]
  LED1 = LED - 5mm [color="Red (633nm)" package="5 mm [THT]"]
  S1 = Pushbutton [package="[THT]"]
  S2 = Pushbutton [package="[THT]"]
  R2 = Resistor [tolerance=±5% resistance=10k package=THT]
  R3 = Resistor [tolerance=±5% resistance=330 package=THT]

nets:
  3V3: Raspberry_Pi1.3v3, IC1.VCC, R2.Pin_0
  N1: Raspberry_Pi1.GPIO17, IC1.D0_1, S2.Pin_3, S2.Pin_4
  N2: Raspberry_Pi1.GPIO23, IC1.D0_0/RESET, S1.Pin_3, S1.Pin_4, R2.Pin_1
  N3: Raspberry_Pi1.GPIO15, IC1.D1_7/TXD
  N4: Raspberry_Pi1.GPIO14, IC1.D1_6/RXD
  GND: Raspberry_Pi1.GND, IC1.GND, LED1.cathode, S1.Pin_1, S1.Pin_2, R3.Pin_0
  N5: IC1.D1_5, R1.Pin_0
  N6: R1.Pin_1, LED1.anode
  N7: S2.Pin_1, S2.Pin_2, R3.Pin_1
